// Logisim project  Casio X Ayzek.circ as structural Verilog: 5 circuits, main circuit main
module main (
  input  in_1,
  output [3:0] out_2
);

  wire \_59_сек , A, A_out, AB_out, \am_pm_1бит , \am_pm_будильник_1бит , and_1_out, and_2_out, and_3_out,
       and_4_out, and_5_out, and_6_out, and_7_out, and_8_out, and_9_out, and_10_out, and_11_out, and_12_out,
       and_13_out, and_14_out, and_15_out, and_16_out, and_17_out, and_18_out, and_19_out, and_21_out,
       and_22_out, and_23_out, and_24_out, and_25_out, and_26_out, and_27_out, and_28_out, and_29_out,
       and_30_out, and_31_out, and_32_out, and_33_out, and_34_out, and_35_out, and_36_out, and_37_out,
       and_38_out, and_39_out, and_40_out, and_41_out, and_42_out, and_43_out, and_44_out, and_45_out,
       and_46_out, and_47_out, and_48_out, and_49_out, and_50_out, and_51_out, and_52_out, and_53_out,
       and_54_out, and_55_out, and_56_out, and_57_out, and_58_out, and_59_out, and_60_out, and_61_out,
       and_62_out, and_63_out, and_64_out, and_65_out, and_66_out, and_72_out, and_73_out, and_79_out,
       and_80_out, and_81_out, and_82_out, and_83_out, and_84_out, and_85_out, and_86_out, and_87_out,
       and_88_out, and_89_out, and_90_out, and_91_out, and_92_out, and_93_out, and_95_out, and_96_out,
       and_97_out, and_98_out, and_99_out, and_100_out, and_101_out, and_102_out, and_103_out, and_104_out,
       and_107_out, and_108_out, and_109_out, and_110_out, and_111_out, and_112_out, B, B_out,
       comparator_1_eq, comparator_2_eq, comparator_3_eq, comparator_4_eq, comparator_5_eq, comparator_6_eq,
       comparator_7_eq, comparator_8_eq, comparator_9_eq, comparator_11_eq, comparator_12_eq,
       comparator_13_eq, comparator_14_eq, comparator_15_eq, comparator_16_eq, counter_4_q, counter_8_q,
       d_ff_1_q, d_ff_2_q, d_ff_7_q, d_ff_8_q, i1, i2, i3, i4, i5, i6, i7, i8, i9, i10, i11, L1, L2, L3, L6,
       L7, L8, L9, L10, L11, L45, not_1_out, not_2_out, or_1_out, or_2_out, or_3_out, or_4_out, or_5_out,
       or_6_out, or_7_out, or_8_out, or_10_out, or_11_out, or_12_out, or_13_out, or_14_out, or_15_out,
       or_18_out, or_19_out, or_20_out, or_28_out, Q1_out, Q2_out, Q3_out, Q4_out, \будильник_активность ,
       \звук , \откл_буд , \сигнал_будильника , \такт ;
  wire [2:0] counter_7_q;
  wire [3:0] counter_9_q, \день1_верх , \день1_низ , \день2_верх , \день2_низ , \дес_мин_будильник_4бит ,
       \дес_мин_секундомер_4бит , \дес_сек_секундомер_4бит , \дес_час_будильник_4бит ,
       \ед_мин_будильник_4бит , \ед_мин_секундомер_4бит , \ед_сек_секундомер_4бит , \ед_час_будильник_4бит ,
       \мин_дес_верх , \мин_дес_низ , \мин_ед_верх , \мин_ед_низ , \мин_сек_дес_верх , \мин_сек_дес_низ ,
       \мин_сек_ед_верх , \мин_сек_ед_низ , \минуты_дес_4бит , \минуты_ед_4бит , \сегмент1_1_верх ,
       \сегмент1_1_низ , \сегмент1_2_верх , \сегмент1_2_низ , \сегмент2_1_верх , \сегмент2_1_низ ,
       \сегмент2_2_верх , \сегмент2_2_низ , \сегмент3_1_верх , \сегмент3_1_низ , \сегмент3_2_верх ,
       \сегмент3_2_низ , \сегмент4_1_верх , \сегмент4_1_низ , \сегмент4_2_верх , \сегмент4_2_низ ,
       \сек_сек_дес_верх , \сек_сек_дес_низ , \сек_сек_ед_верх , \сек_сек_ед_низ , \часы_дес_4бит ,
       \часы_дес_верх , \часы_дес_низ , \часы_ед_4бит , \часы_ед_верх , \часы_ед_низ ;
  wire [7:0] \мин_буд_десятки , \мин_буд_единицы , \секунды_8бит , \час_буд_десятки , \час_буд_единицы ;
  wire [15:0] am_pm, \am_pm_будильник ;

  Clock clock_1 (.out(\такт ));
  and and_1 (and_1_out, \секунды_8бит [0], \секунды_8бит [1], ~\секунды_8бит [2], \секунды_8бит [3]);  // AND_Gate
  and and_2 (and_2_out, \секунды_8бит [4], \секунды_8бит [5], ~\секунды_8бит [6], ~\секунды_8бит [7]);  // AND_Gate
  and and_3 (and_3_out, \минуты_ед_4бит [0], ~\минуты_ед_4бит [1], ~\минуты_ед_4бит [2], \минуты_ед_4бит [3]);  // AND_Gate
  and and_4 (and_4_out, \минуты_ед_4бит [0], ~\минуты_ед_4бит [1], ~\минуты_ед_4бит [2], \минуты_ед_4бит [3]);  // AND_Gate
  and and_5 (and_5_out, \минуты_дес_4бит [0], ~\минуты_дес_4бит [1], \минуты_дес_4бит [2], ~\минуты_дес_4бит [3]);  // AND_Gate
  and and_6 (and_6_out, ~\часы_ед_4бит [0], \часы_ед_4бит [1], ~\часы_ед_4бит [2], ~\часы_ед_4бит [3]);  // AND_Gate
  and and_7 (and_7_out, \часы_дес_4бит [0], ~\часы_дес_4бит [1], ~\часы_дес_4бит [2], ~\часы_дес_4бит [3]);  // AND_Gate
  and and_8 (and_8_out, \часы_ед_4бит [0], ~\часы_ед_4бит [1], ~\часы_ед_4бит [2], \часы_ед_4бит [3]);  // AND_Gate
  and and_9 (and_9_out, \минуты_ед_4бит [0], ~\минуты_ед_4бит [1], ~\минуты_ед_4бит [2], \минуты_ед_4бит [3]);  // AND_Gate
  and and_10 (and_10_out, \минуты_дес_4бит [0], ~\минуты_дес_4бит [1], \минуты_дес_4бит [2], ~\минуты_дес_4бит [3]);  // AND_Gate
  and and_11 (and_11_out, ~\часы_ед_4бит [0], \часы_ед_4бит [1], ~\часы_ед_4бит [2], ~\часы_ед_4бит [3]);  // AND_Gate
  and and_12 (and_12_out, and_11_out, and_13_out);
  and and_13 (and_13_out, \часы_дес_4бит [0], ~\часы_дес_4бит [1], ~\часы_дес_4бит [2], ~\часы_дес_4бит [3]);  // AND_Gate
  and and_14 (and_14_out, \минуты_ед_4бит [0], ~\минуты_ед_4бит [1], ~\минуты_ед_4бит [2], \минуты_ед_4бит [3]);  // AND_Gate
  and and_15 (and_15_out, \минуты_дес_4бит [0], ~\минуты_дес_4бит [1], \минуты_дес_4бит [2], ~\минуты_дес_4бит [3]);  // AND_Gate
  and and_16 (and_16_out, \часы_ед_4бит [0], ~\часы_ед_4бит [1], ~\часы_ед_4бит [2], ~\часы_ед_4бит [3]);  // AND_Gate
  and and_17 (and_17_out, \часы_дес_4бит [0], ~\часы_дес_4бит [1], ~\часы_дес_4бит [2], ~\часы_дес_4бит [3]);  // AND_Gate
  and and_18 (and_18_out, ~\часы_ед_4бит [0], ~\часы_ед_4бит [1], ~\часы_ед_4бит [2], ~\часы_ед_4бит [3]);  // AND_Gate
  and and_19 (and_19_out, ~\часы_дес_4бит [0], ~\часы_дес_4бит [1], ~\часы_дес_4бит [2], ~\часы_дес_4бит [3]);  // AND_Gate
  or or_1 (or_1_out, A, B);
  not not_1 (not_1_out, or_1_out);
  and and_20 (\_59_сек , and_1_out, and_2_out);
  and and_21 (and_21_out, and_3_out, \_59_сек );
  D_Flip_Flop d_ff_1 (.clk(i4), .D(and_3_out), .Q(d_ff_1_q), .reset(d_ff_1_q));  // open: Qn, preset, en
  and and_22 (and_22_out, \_59_сек , and_4_out, and_5_out);
  and and_23 (and_23_out, and_6_out, and_7_out);
  and and_24 (and_24_out, \_59_сек , and_8_out, and_9_out, and_10_out);
  D_Flip_Flop d_ff_2 (.clk(i3), .D(and_8_out), .Q(d_ff_2_q), .reset(d_ff_2_q));  // open: Qn, preset, en
  and and_25 (and_25_out, \_59_сек , and_14_out, and_15_out, and_16_out, and_17_out);
  and and_26 (and_26_out, and_18_out, and_19_out, i3);
  not not_2 (not_2_out, not_1_out);
  and and_27 (and_27_out, A, out_2[3], ~out_2[2], out_2[1]);  // AND_Gate
  and and_28 (and_28_out, B, out_2[3], ~out_2[2], out_2[1]);  // AND_Gate
  and and_29 (and_29_out, A, ~B, out_2[3], out_2[2], ~out_2[1]);  // AND_Gate
  and and_30 (and_30_out, A, ~B, out_2[3], ~out_2[1], out_2[0]);  // AND_Gate
  and and_31 (and_31_out, B, out_2[3], out_2[2], ~out_2[1], out_2[0]);  // AND_Gate
  and and_32 (and_32_out, ~A, B, out_2[2], ~out_2[1], out_2[0]);  // AND_Gate
  and and_33 (and_33_out, ~A, B, out_2[3], out_2[2], ~out_2[1]);  // AND_Gate
  and and_34 (and_34_out, ~A, B, out_2[3], ~out_2[1], out_2[0]);  // AND_Gate
  and and_35 (and_35_out, A, ~B, ~out_2[3], out_2[2], out_2[1], out_2[0]);  // AND_Gate
  and and_36 (and_36_out, ~A, B, ~out_2[3], out_2[2], out_2[1], ~out_2[0]);  // AND_Gate
  and and_37 (and_37_out, A, ~B, out_2[2], ~out_2[1]);  // AND_Gate
  and and_38 (and_38_out, ~A, B, out_2[2], ~out_2[1]);  // AND_Gate
  and and_39 (and_39_out, A, ~B, ~out_2[3], out_2[1], ~out_2[0]);  // AND_Gate
  and and_40 (and_40_out, A, out_2[3], ~out_2[2], ~out_2[1], ~out_2[0]);  // AND_Gate
  and and_41 (and_41_out, A, B, out_2[3], ~out_2[2], ~out_2[1]);  // AND_Gate
  and and_42 (and_42_out, B, ~out_2[3], out_2[2], out_2[1], out_2[0]);  // AND_Gate
  and and_43 (and_43_out, ~A, B, ~out_2[2], out_2[1], out_2[0]);  // AND_Gate
  and and_44 (and_44_out, B, out_2[3], ~out_2[2], ~out_2[1], ~out_2[0]);  // AND_Gate
  and and_45 (and_45_out, A, ~B, ~out_2[2], out_2[1]);  // AND_Gate
  and and_46 (and_46_out, A, B, ~out_2[3], out_2[2]);  // AND_Gate
  and and_47 (and_47_out, ~A, B, ~out_2[2], ~out_2[0]);  // AND_Gate
  and and_48 (and_48_out, B, out_2[3], ~out_2[2], ~out_2[1]);  // AND_Gate
  and and_49 (and_49_out, A, ~B, ~out_2[3], out_2[1], ~out_2[0]);  // AND_Gate
  and and_50 (and_50_out, A, ~B, out_2[3], ~out_2[2], ~out_2[0]);  // AND_Gate
  and and_51 (and_51_out, A, B, out_2[3], ~out_2[1], ~out_2[0]);  // AND_Gate
  and and_52 (and_52_out, A, ~out_2[3], ~out_2[2], out_2[1], out_2[0]);  // AND_Gate
  and and_53 (and_53_out, B, ~out_2[3], out_2[2], out_2[1], out_2[0]);  // AND_Gate
  and and_54 (and_54_out, B, out_2[3], ~out_2[2], out_2[1]);  // AND_Gate
  and and_55 (and_55_out, A, ~B, out_2[2], ~out_2[1], out_2[0]);  // AND_Gate
  and and_56 (and_56_out, A, ~B, ~out_2[2], out_2[1], out_2[0]);  // AND_Gate
  and and_57 (and_57_out, A, ~B, out_2[3], ~out_2[1], out_2[0]);  // AND_Gate
  and and_58 (and_58_out, A, ~B, ~out_2[2], ~out_2[1], ~out_2[0]);  // AND_Gate
  and and_59 (and_59_out, A, B, ~out_2[3], ~out_2[2], ~out_2[1]);  // AND_Gate
  and and_60 (and_60_out, ~A, B, ~out_2[3], out_2[2], ~out_2[0]);  // AND_Gate
  and and_61 (and_61_out, ~A, B, ~out_2[3], out_2[2], out_2[1]);  // AND_Gate
  and and_62 (and_62_out, ~A, B, ~out_2[3], out_2[1], ~out_2[0]);  // AND_Gate
  and and_63 (and_63_out, B, ~out_2[3], ~out_2[2], ~out_2[1], out_2[0]);  // AND_Gate
  and and_64 (and_64_out, B, out_2[3], out_2[2], ~out_2[1], out_2[0]);  // AND_Gate
  and and_65 (and_65_out, ~A, B, out_2[3], ~out_2[2], ~out_2[0]);  // AND_Gate
  and and_66 (and_66_out, A, ~B, ~out_2[3], out_2[2], out_2[1], ~out_2[0]);  // AND_Gate
  and and_67 (i1, A, ~B, ~out_2[3], ~out_2[2], ~out_2[1], out_2[0]);  // AND_Gate
  and and_68 (i2, A, ~B, ~out_2[3], ~out_2[2], out_2[1], out_2[0]);  // AND_Gate
  and and_69 (i3, A, ~B, ~out_2[3], out_2[2], ~out_2[1], ~out_2[0]);  // AND_Gate
  and and_70 (i4, A, ~B, ~out_2[3], out_2[2], ~out_2[1], out_2[0]);  // AND_Gate
  and and_71 (i5, A, ~B, out_2[3], ~out_2[2], ~out_2[1], ~out_2[0]);  // AND_Gate
  and and_72 (and_72_out, ~A, B, ~out_2[3], out_2[2], out_2[1], out_2[0]);  // AND_Gate
  and and_73 (and_73_out, ~A, B, out_2[3], ~out_2[2], ~out_2[1], ~out_2[0]);  // AND_Gate
  and and_74 (i7, A, ~B, out_2[3], ~out_2[2], ~out_2[1], out_2[0]);  // AND_Gate
  and and_75 (i8, A, ~B, out_2[3], ~out_2[2], out_2[1], ~out_2[0]);  // AND_Gate
  and and_76 (i9, A, ~B, out_2[3], ~out_2[2], out_2[1], out_2[0]);  // AND_Gate
  and and_77 (i10, A, ~B, out_2[3], out_2[2], ~out_2[1], ~out_2[0]);  // AND_Gate
  and and_78 (i11, A, ~B, out_2[3], out_2[2], ~out_2[1], out_2[0]);  // AND_Gate
  or or_2 (or_2_out, \_59_сек , i4);
  or or_3 (or_3_out, i4, \такт );
  or or_4 (or_4_out, and_21_out, and_79_out);
  and and_79 (and_79_out, d_ff_1_q, i4);
  or or_5 (or_5_out, and_23_out, in_1);
  or or_6 (or_6_out, and_24_out, and_80_out);
  and and_80 (and_80_out, d_ff_2_q, i3);
  or or_7 (or_7_out, and_12_out, in_1);
  or or_8 (or_8_out, and_25_out, i10, and_26_out);
  or or_9 (i6, and_72_out, and_73_out);
  Counter #(.max('h3b)) counter_1 (
    .D({8{1'b0}}), .count(1'b1), .Q(\секунды_8бит ), .clk(\такт ), .clr(in_1));  // open: load, carry
  Counter #(.width(4), .max('h9)) counter_2 (
    .D(4'b0000), .count(or_2_out), .Q(\минуты_ед_4бит ), .clk(or_3_out), .clr(in_1));  // open: load, carry
  or or_10 (or_10_out, and_79_out, \такт );
  or or_11 (or_11_out, and_22_out, i3);
  or or_12 (or_12_out, i3, \такт );
  Counter #(.width(4), .max('h2)) counter_3 (
    .D(4'b0000), .count(or_6_out), .Q(\часы_дес_4бит ), .clk(or_13_out), .clr(or_7_out));  // open: load, carry
  or or_13 (or_13_out, and_80_out, \такт );
  not not_3 (\am_pm_1бит , counter_4_q);
  Counter #(.width(1), .max('h1)) counter_4 (
    .D(1'b0), .count(or_8_out), .Q(counter_4_q), .clk(or_8_out), .clr(in_1));  // open: load, carry
  or Q3 (Q3_out, and_46_out, and_47_out, and_48_out, and_49_out, and_45_out, and_50_out, and_51_out, and_52_out, and_53_out);
  or Q4 (Q4_out, and_54_out, and_55_out, and_56_out, and_57_out, and_58_out, and_59_out, and_60_out, and_61_out, and_62_out, and_63_out, and_64_out, and_65_out, and_66_out);
  NUM NUM (.x(\минуты_ед_4бит ), .y({\мин_ед_верх , \мин_ед_низ }));
  NUM NUM_2 (.x(\минуты_дес_4бит ), .y({\мин_дес_верх , \мин_дес_низ }));
  Counter #(.width(4), .max('h5)) counter_5 (
    .D(4'b0000), .count(or_4_out), .Q(\минуты_дес_4бит ), .clk(or_10_out), .clr(in_1));  // open: load, carry
  Counter #(.width(4), .max('h9)) counter_6 (
    .D(4'b0000), .count(or_11_out), .Q(\часы_ед_4бит ), .clk(or_12_out), .clr(or_5_out));  // open: load, carry
  NUM NUM_3 (.x(\часы_ед_4бит ), .y({\часы_ед_верх , \часы_ед_низ }));
  NUM NUM_4 (.x(\часы_дес_4бит ), .y({\часы_дес_верх , \часы_дес_низ }));
  or or_14 (or_14_out, and_81_out, i2);
  and and_81 (and_81_out, \am_pm_1бит , and_25_out);
  or Q1 (Q1_out, and_27_out, and_28_out, and_29_out, and_30_out, and_31_out, and_32_out, and_33_out, and_34_out, and_35_out, and_36_out);
  or Q2 (Q2_out, and_37_out, and_38_out, and_39_out, and_40_out, and_41_out, and_42_out, and_43_out, and_44_out);
  am_and_pm u_AM_PM (.x(\am_pm_1бит ), .y(am_pm));
  Counter #(.width(3), .max('h6)) counter_7 (
    .D(3'b000), .count(or_14_out), .Q(counter_7_q), .clk(or_15_out), .clr(in_1));  // open: load, carry
  or or_15 (or_15_out, i2, \такт );
  D_Flip_Flop d_ff_3 (.clk(not_2_out), .D(Q1_out), .Q(out_2[3]));  // open: Qn, preset, en, reset
  D_Flip_Flop d_ff_4 (.clk(not_2_out), .D(Q2_out), .Q(out_2[2]));  // open: Qn, preset, en, reset
  D_Flip_Flop d_ff_5 (.clk(not_2_out), .D(Q3_out), .Q(out_2[1]));  // open: Qn, preset, en, reset
  D_Flip_Flop d_ff_6 (.clk(not_2_out), .D(Q4_out), .Q(out_2[0]));  // open: Qn, preset, en, reset
  DAY DAY (.x(counter_7_q), .y({\день1_верх , \день1_низ , \день2_верх , \день2_низ }));
  Button AB (.out(AB_out));
  or or_16 (A, AB_out, A_out);
  Button u_A (.out(A_out));
  or or_17 (B, AB_out, B_out);
  Button u_B (.out(B_out));
  and and_82 (and_82_out, i6, counter_8_q);
  and and_83 (and_83_out, \сигнал_будильника , \будильник_активность );
  or or_18 (or_18_out, i7, \откл_буд );
  _7_Segment_Display u_7_segment_display_1 (
    .g(\сегмент1_1_верх [3]), .f(\сегмент1_1_верх [2]), .a(\сегмент1_1_верх [1]), .b(\сегмент1_1_верх [0]),
    .e(\сегмент1_1_низ [3]), .d(\сегмент1_1_низ [2]), .c(\сегмент1_1_низ [1]), .dp(\сегмент1_1_низ [0]));
  LED led_1 (.in(\звук ));
  and and_84 (and_84_out, and_83_out, \такт );
  Comparator #(.width(4)) comparator_1 (
    .a(\ед_мин_будильник_4бит ), .b(4'b1001), .eq(comparator_1_eq));  // open: gt, lt
  Comparator #(.width(4)) comparator_2 (
    .a(\ед_час_будильник_4бит ), .b(4'b1001), .eq(comparator_2_eq));  // open: gt, lt
  _7_Segment_Display u_7_segment_display_2 (
    .g(\сегмент4_1_верх [3]), .f(\сегмент4_1_верх [2]), .a(\сегмент4_1_верх [1]), .b(\сегмент4_1_верх [0]),
    .e(\сегмент4_1_низ [3]), .d(\сегмент4_1_низ [2]), .c(\сегмент4_1_низ [1]), .dp(\сегмент4_1_низ [0]));
  _7_Segment_Display u_7_segment_display_3 (
    .g(\сегмент4_2_верх [3]), .f(\сегмент4_2_верх [2]), .a(\сегмент4_2_верх [1]), .b(\сегмент4_2_верх [0]),
    .e(\сегмент4_2_низ [3]), .d(\сегмент4_2_низ [2]), .c(\сегмент4_2_низ [1]), .dp(\сегмент4_2_низ [0]));
  Counter #(.width(1), .max('h1)) counter_8 (
    .D(1'b0), .count(or_19_out), .Q(counter_8_q), .clk(or_19_out));  // open: load, carry, clr
  or or_19 (or_19_out, i5, and_82_out);
  Comparator #(.width(4)) comparator_3 (
    .a(\ед_сек_секундомер_4бит ), .b(4'b1001), .eq(comparator_3_eq));  // open: gt, lt
  Comparator #(.width(4)) comparator_4 (
    .a(\дес_сек_секундомер_4бит ), .b(4'b0101), .eq(comparator_4_eq));  // open: gt, lt
  Comparator #(.width(4)) comparator_5 (
    .a(\ед_сек_секундомер_4бит ), .b(4'b1001), .eq(comparator_5_eq));  // open: gt, lt
  Comparator #(.width(4)) comparator_6 (
    .a(\дес_сек_секундомер_4бит ), .b(4'b0101), .eq(comparator_6_eq));  // open: gt, lt
  Comparator #(.width(4)) comparator_7 (
    .a(\ед_мин_секундомер_4бит ), .b(4'b1001), .eq(comparator_7_eq));  // open: gt, lt
  Counter #(.width(4), .max('ha)) counter_9 (
    .D(4'b0000), .count(and_84_out), .Q(counter_9_q), .clk(and_84_out), .clr(\откл_буд ));  // open: load, carry
  Counter #(.width(1), .max('h1)) counter_10 (
    .D(1'b0), .count(or_18_out), .Q(\будильник_активность ), .clk(or_18_out));  // open: load, carry, clr
  Comparator #(.width(4)) comparator_8 (
    .a(\дес_час_будильник_4бит ), .b(4'b0001), .eq(comparator_8_eq));  // open: gt, lt
  Comparator #(.width(4)) comparator_9 (
    .a(\ед_час_будильник_4бит ), .b(4'b0010), .eq(comparator_9_eq));  // open: gt, lt
  Counter #(.width(1), .max('h1)) counter_11 (
    .D(1'b0), .count(i11), .Q(\am_pm_будильник_1бит ), .clk(i11));  // open: load, carry, clr
  _7_Segment_Display u_7_segment_display_4 (
    .g(\сегмент1_2_верх [3]), .f(\сегмент1_2_верх [2]), .a(\сегмент1_2_верх [1]), .b(\сегмент1_2_верх [0]),
    .e(\сегмент1_2_низ [3]), .d(\сегмент1_2_низ [2]), .c(\сегмент1_2_низ [1]), .dp(\сегмент1_2_низ [0]));
  and and_85 (and_85_out, \такт , counter_8_q);
  and and_86 (and_86_out, comparator_3_eq, comparator_4_eq);
  and and_87 (and_87_out, comparator_5_eq, comparator_6_eq, comparator_7_eq);
  Comparator #(.width(4)) comparator_10 (.a(counter_9_q), .b(4'b1010), .eq(\откл_буд ), .lt(\звук ));  // open: gt
  D_Flip_Flop d_ff_7 (.clk(i9), .D(comparator_1_eq), .Q(d_ff_7_q), .reset(d_ff_7_q));  // open: Qn, preset, en
  and and_88 (and_88_out, i8, comparator_8_eq, comparator_9_eq);
  D_Flip_Flop d_ff_8 (.clk(i8), .D(comparator_2_eq), .Q(d_ff_8_q), .reset(d_ff_8_q));  // open: Qn, preset, en
  _7_Segment_Display u_7_segment_display_5 (
    .g(\сегмент2_1_верх [3]), .f(\сегмент2_1_верх [2]), .a(\сегмент2_1_верх [1]), .b(\сегмент2_1_верх [0]),
    .e(\сегмент2_1_низ [3]), .d(\сегмент2_1_низ [2]), .c(\сегмент2_1_низ [1]), .dp(\сегмент2_1_низ [0]));
  and and_89 (and_89_out, i9, d_ff_7_q);
  and and_90 (and_90_out, i8, d_ff_8_q);
  am_and_pm am_and_pm_1 (.x(\am_pm_будильник_1бит ), .y(\am_pm_будильник ));
  _7_Segment_Display u_7_segment_display_6 (
    .g(\сегмент2_2_верх [3]), .f(\сегмент2_2_верх [2]), .a(\сегмент2_2_верх [1]), .b(\сегмент2_2_верх [0]),
    .e(\сегмент2_2_низ [3]), .d(\сегмент2_2_низ [2]), .c(\сегмент2_2_низ [1]), .dp(\сегмент2_2_низ [0]));
  Comparator #(.width(4)) comparator_11 (
    .a(\ед_сек_секундомер_4бит ), .b(4'b1001), .eq(comparator_11_eq));  // open: gt, lt
  Counter #(.width(4), .max('h9)) counter_12 (
    .count(i9), .Q(\ед_мин_будильник_4бит ), .clk(or_20_out));  // open: load, D, carry, clr
  or or_20 (or_20_out, i9, and_89_out);
  Counter #(.width(4), .max('h5)) counter_13 (
    .count(and_89_out), .Q(\дес_мин_будильник_4бит ), .clk(and_89_out));  // open: load, D, carry, clr
  Counter #(.width(4), .max('h9)) counter_14 (
    .count(i8), .Q(\ед_час_будильник_4бит ), .clk(i8), .clr(and_88_out));  // open: load, D, carry
  Counter #(.width(4), .max('h2)) counter_15 (
    .count(and_90_out), .Q(\дес_час_будильник_4бит ), .clk(and_90_out), .clr(and_88_out));  // open: load, D, carry
  and and_91 (and_91_out, ~out_2[3], out_2[1], ~out_2[0]);  // AND_Gate
  and and_92 (and_92_out, ~out_2[3], ~out_2[2], out_2[1]);  // AND_Gate
  and and_93 (and_93_out, ~out_2[3], ~out_2[2], ~out_2[0]);  // AND_Gate
  and and_94 (L2, ~out_2[3], ~out_2[0]);  // AND_Gate
  and and_95 (and_95_out, ~out_2[3], out_2[1], ~out_2[0]);  // AND_Gate
  and and_96 (and_96_out, ~out_2[3], ~out_2[2], ~out_2[0]);  // AND_Gate
  and and_97 (and_97_out, ~out_2[3], out_2[2], ~out_2[1], out_2[0]);  // AND_Gate
  and and_98 (and_98_out, ~out_2[3], out_2[1], ~out_2[0]);  // AND_Gate
  and and_99 (and_99_out, ~out_2[3], ~out_2[2], ~out_2[0]);  // AND_Gate
  and and_100 (and_100_out, out_2[3], out_2[2], ~out_2[1], ~out_2[0]);  // AND_Gate
  and and_101 (and_101_out, out_2[3], ~out_2[2], ~out_2[1], ~out_2[0]);  // AND_Gate
  and and_102 (and_102_out, ~out_2[3], out_2[2], out_2[1], out_2[0]);  // AND_Gate
  and and_103 (and_103_out, out_2[3], ~out_2[2], out_2[1], ~out_2[0]);  // AND_Gate
  and and_104 (and_104_out, out_2[3], ~out_2[2], ~out_2[1], out_2[0]);  // AND_Gate
  and and_105 (L7, out_2[3], ~out_2[2], out_2[0]);  // AND_Gate
  and and_106 (L11, out_2[3], ~out_2[1], out_2[0]);  // AND_Gate
  and and_107 (and_107_out, out_2[2], ~out_2[1], ~out_2[0]);  // AND_Gate
  and and_108 (and_108_out, ~out_2[3], out_2[2], ~out_2[1]);  // AND_Gate
  and and_109 (and_109_out, ~out_2[3], ~out_2[2], out_2[1]);  // AND_Gate
  and and_110 (and_110_out, out_2[3], ~out_2[2]);  // AND_Gate
  and and_111 (and_111_out, out_2[3], ~out_2[1], out_2[0]);  // AND_Gate
  and and_112 (and_112_out, ~out_2[3], out_2[2], out_2[1]);  // AND_Gate
  Counter #(.width(4), .max('h9)) counter_16 (
    .count(1'b1), .Q(\ед_сек_секундомер_4бит ), .clk(and_85_out), .clr(i6));  // open: load, D, carry
  Counter #(.width(4), .max('h5)) counter_17 (
    .count(comparator_11_eq), .Q(\дес_сек_секундомер_4бит ), .clk(and_85_out), .clr(i6));  // open: load, D, carry
  Counter #(.width(4), .max('h9)) counter_18 (
    .count(and_86_out), .Q(\ед_мин_секундомер_4бит ), .clk(and_85_out), .clr(i6));  // open: load, D, carry
  Counter #(.width(4), .max('h5)) counter_19 (
    .count(and_87_out), .Q(\дес_мин_секундомер_4бит ), .clk(and_85_out), .clr(i6));  // open: load, D, carry
  NUM num_5 (.x(\ед_мин_будильник_4бит ), .y(\мин_буд_единицы ));
  NUM num_6 (.x(\дес_мин_будильник_4бит ), .y(\мин_буд_десятки ));
  NUM num_7 (.x(\ед_час_будильник_4бит ), .y(\час_буд_единицы ));
  NUM num_8 (.x(\дес_час_будильник_4бит ), .y(\час_буд_десятки ));
  NUM num_9 (.x(\ед_сек_секундомер_4бит ), .y({\сек_сек_ед_верх , \сек_сек_ед_низ }));
  NUM num_10 (.x(\дес_сек_секундомер_4бит ), .y({\сек_сек_дес_верх , \сек_сек_дес_низ }));
  NUM num_11 (.x(\ед_мин_секундомер_4бит ), .y({\мин_сек_ед_верх , \мин_сек_ед_низ }));
  NUM num_12 (.x(\дес_мин_секундомер_4бит ), .y({\мин_сек_дес_верх , \мин_сек_дес_низ }));
  or or_21 (L1, and_91_out, and_92_out, and_93_out);
  or or_22 (L3, and_95_out, and_96_out, and_97_out);
  or or_23 (L10, and_98_out, and_99_out, and_100_out);
  or or_24 (L45, and_101_out, and_102_out);
  or or_25 (L6, and_103_out, and_104_out);
  or or_26 (L8, and_107_out, and_108_out, and_109_out);
  or or_27 (L9, and_110_out, and_111_out, and_112_out);
  LED led_2 (.in(L8));
  LED led_3 (.in(L9));
  LED led_4 (.in(\будильник_активность ));
  _7_Segment_Display u_7_segment_display_7 (
    .g(\сегмент3_1_верх [3]), .f(\сегмент3_1_верх [2]), .a(\сегмент3_1_верх [1]), .b(\сегмент3_1_верх [0]),
    .e(\сегмент3_1_низ [3]), .d(\сегмент3_1_низ [2]), .c(\сегмент3_1_низ [1]), .dp(\сегмент3_1_низ [0]));
  _7_Segment_Display u_7_segment_display_8 (
    .g(\сегмент3_2_верх [3]), .f(\сегмент3_2_верх [2]), .a(\сегмент3_2_верх [1]), .b(\сегмент3_2_верх [0]),
    .e(\сегмент3_2_низ [3]), .d(\сегмент3_2_низ [2]), .c(\сегмент3_2_низ [1]), .dp(\сегмент3_2_низ [0]));
  Comparator #(.width(4)) comparator_12 (
    .a(\ед_мин_будильник_4бит ), .b(\минуты_ед_4бит ), .eq(comparator_12_eq));  // open: gt, lt
  Comparator #(.width(4)) comparator_13 (
    .a(\дес_мин_будильник_4бит ), .b(\минуты_дес_4бит ), .eq(comparator_13_eq));  // open: gt, lt
  Comparator #(.width(4)) comparator_14 (
    .a(\ед_час_будильник_4бит ), .b(\часы_ед_4бит ), .eq(comparator_14_eq));  // open: gt, lt
  Comparator #(.width(4)) comparator_15 (
    .a(\дес_час_будильник_4бит ), .b(\часы_дес_4бит ), .eq(comparator_15_eq));  // open: gt, lt
  Comparator #(.width(1)) comparator_16 (
    .a(\am_pm_будильник_1бит ), .b(\am_pm_1бит ), .eq(comparator_16_eq));  // open: gt, lt
  and and_113 (\сигнал_будильника , comparator_12_eq, comparator_13_eq, comparator_14_eq, comparator_15_eq, comparator_16_eq);
  assign \сегмент1_1_верх  = L2 ? \часы_дес_верх  : 4'bz;  // Controlled_Buffer controlled_buffer_1
  assign \сегмент1_1_низ  = L2 ? \часы_дес_низ  : 4'bz;  // Controlled_Buffer controlled_buffer_2
  assign \сегмент1_1_верх  = L45 ? \мин_сек_дес_верх  : 4'bz;  // Controlled_Buffer controlled_buffer_3
  assign \сегмент1_1_низ  = L45 ? \мин_сек_дес_низ  : 4'bz;  // Controlled_Buffer controlled_buffer_4
  assign \сегмент3_1_верх  = L1 ? \день1_верх  : 4'bz;  // Controlled_Buffer controlled_buffer_5
  assign \сегмент3_1_низ  = L1 ? \день1_низ  : 4'bz;  // Controlled_Buffer controlled_buffer_6
  assign \сегмент3_1_верх  = or_28_out ? 4'b0000 : 4'bz;  // Controlled_Buffer controlled_buffer_7
  assign \сегмент3_1_низ  = or_28_out ? 4'b0000 : 4'bz;  // Controlled_Buffer controlled_buffer_8
  assign \сегмент1_1_верх  = L6 ? \час_буд_десятки [7:4] : 4'bz;  // Controlled_Buffer controlled_buffer_9
  assign \сегмент1_1_низ  = L6 ? \час_буд_десятки [3:0] : 4'bz;  // Controlled_Buffer controlled_buffer_10
  or or_28 (or_28_out, L45, L6, L7);
  assign \сегмент1_2_верх  = L2 ? \часы_ед_верх  : 4'bz;  // Controlled_Buffer controlled_buffer_11
  assign \сегмент1_2_низ  = L2 ? \часы_ед_низ  : 4'bz;  // Controlled_Buffer controlled_buffer_12
  assign \сегмент3_2_верх  = L1 ? \день2_верх  : 4'bz;  // Controlled_Buffer controlled_buffer_13
  assign \сегмент3_2_низ  = L1 ? \день2_низ  : 4'bz;  // Controlled_Buffer controlled_buffer_14
  assign \сегмент1_2_верх  = L45 ? \мин_сек_ед_верх  : 4'bz;  // Controlled_Buffer controlled_buffer_15
  assign \сегмент1_2_низ  = L45 ? \мин_сек_ед_низ  : 4'bz;  // Controlled_Buffer controlled_buffer_16
  assign \сегмент3_2_верх  = or_28_out ? 4'b0000 : 4'bz;  // Controlled_Buffer controlled_buffer_17
  assign \сегмент3_2_низ  = or_28_out ? 4'b0000 : 4'bz;  // Controlled_Buffer controlled_buffer_18
  assign \сегмент1_2_верх  = L6 ? \час_буд_единицы [7:4] : 4'bz;  // Controlled_Buffer controlled_buffer_19
  assign \сегмент1_2_низ  = L6 ? \час_буд_единицы [3:0] : 4'bz;  // Controlled_Buffer controlled_buffer_20
  assign \сегмент4_1_верх  = L10 ? am_pm[15:12] : 4'bz;  // Controlled_Buffer controlled_buffer_21
  assign \сегмент4_1_низ  = L10 ? am_pm[11:8] : 4'bz;  // Controlled_Buffer controlled_buffer_22
  assign \сегмент2_1_верх  = L3 ? \мин_дес_верх  : 4'bz;  // Controlled_Buffer controlled_buffer_23
  assign \сегмент2_1_низ  = L3 ? \мин_дес_низ  : 4'bz;  // Controlled_Buffer controlled_buffer_24
  assign \сегмент2_1_верх  = L45 ? \сек_сек_дес_верх  : 4'bz;  // Controlled_Buffer controlled_buffer_25
  assign \сегмент2_1_низ  = L45 ? \сек_сек_дес_низ  : 4'bz;  // Controlled_Buffer controlled_buffer_26
  assign \сегмент4_1_верх  = L11 ? \am_pm_будильник [15:12] : 4'bz;  // Controlled_Buffer controlled_buffer_27
  assign \сегмент4_1_низ  = L11 ? \am_pm_будильник [11:8] : 4'bz;  // Controlled_Buffer controlled_buffer_28
  assign \сегмент2_1_верх  = L7 ? \мин_буд_десятки [7:4] : 4'bz;  // Controlled_Buffer controlled_buffer_29
  assign \сегмент2_1_низ  = L7 ? \мин_буд_десятки [3:0] : 4'bz;  // Controlled_Buffer controlled_buffer_30
  assign \сегмент4_2_верх  = L10 ? am_pm[7:4] : 4'bz;  // Controlled_Buffer controlled_buffer_31
  assign \сегмент4_2_низ  = L10 ? am_pm[3:0] : 4'bz;  // Controlled_Buffer controlled_buffer_32
  assign \сегмент2_2_верх  = L3 ? \мин_ед_верх  : 4'bz;  // Controlled_Buffer controlled_buffer_33
  assign \сегмент2_2_низ  = L3 ? \мин_ед_низ  : 4'bz;  // Controlled_Buffer controlled_buffer_34
  assign \сегмент2_2_верх  = L45 ? \сек_сек_ед_верх  : 4'bz;  // Controlled_Buffer controlled_buffer_35
  assign \сегмент2_2_низ  = L45 ? \сек_сек_ед_низ  : 4'bz;  // Controlled_Buffer controlled_buffer_36
  assign \сегмент4_2_верх  = L11 ? \am_pm_будильник [7:4] : 4'bz;  // Controlled_Buffer controlled_buffer_37
  assign \сегмент4_2_низ  = L11 ? \am_pm_будильник [3:0] : 4'bz;  // Controlled_Buffer controlled_buffer_38
  assign \сегмент2_2_верх  = L7 ? \мин_буд_единицы [7:4] : 4'bz;  // Controlled_Buffer controlled_buffer_39
  assign \сегмент2_2_низ  = L7 ? \мин_буд_единицы [3:0] : 4'bz;  // Controlled_Buffer controlled_buffer_40

  // Other names for the same wires on the sheet: q4 = out_2[0]; q3 = out_2[1]; q2 = out_2[2]; q1 = out_2[3];
  //   буква1_буд_верх[3:0] = \am_pm_будильник [15:12]; буква1_буд_низ[3:0] = \am_pm_будильник [11:8];
  //   буква1_верх[3:0] = am_pm[15:12]; буква1_низ[3:0] = am_pm[11:8]; буква2_буд_верх[3:0] = \am_pm_будильник [7:4];
  //   буква2_буд_низ[3:0] = \am_pm_будильник [3:0]; буква2_верх[3:0] = am_pm[7:4]; буква2_низ[3:0] = am_pm[3:0];
  //   день_недели[15:0] = {\день1_верх , \день1_низ , \день2_верх , \день2_низ };
  //   мин_буд_десятки_верх[3:0] = \мин_буд_десятки [7:4]; мин_буд_десятки_низ[3:0] = \мин_буд_десятки [3:0];
  //   мин_буд_единицы_верх[3:0] = \мин_буд_единицы [7:4]; мин_буд_единицы_низ[3:0] = \мин_буд_единицы [3:0];
  //   минуты_десятки[7:0] = {\мин_дес_верх , \мин_дес_низ }; минуты_единицы[7:0] = {\мин_ед_верх , \мин_ед_низ };
  //   мин_сек_десятки[7:0] = {\мин_сек_дес_верх , \мин_сек_дес_низ };
  //   мин_сек_единицы[7:0] = {\мин_сек_ед_верх , \мин_сек_ед_низ };
  //   сек_сек_десятки[7:0] = {\сек_сек_дес_верх , \сек_сек_дес_низ };
  //   сек_сек_единицы[7:0] = {\сек_сек_ед_верх , \сек_сек_ед_низ };
  //   час_буд_десятки_верх[3:0] = \час_буд_десятки [7:4]; час_буд_десятки_низ[3:0] = \час_буд_десятки [3:0];
  //   час_буд_единицы_верх[3:0] = \час_буд_единицы [7:4]; час_буд_единицы_низ[3:0] = \час_буд_единицы [3:0];
  //   часы_десятки[7:0] = {\часы_дес_верх , \часы_дес_низ }; часы_единицы[7:0] = {\часы_ед_верх , \часы_ед_низ }
endmodule

module NUM (
  input  [3:0] x,
  output [7:0] y
);

  wire _0_out, _1_out, _2_out, _3_out, _4_out, _5_out, _6_out, _7_out, _8_out, _9_out;
  wire [7:0] controlled_buffer_1_out, controlled_buffer_2_out, controlled_buffer_3_out,
       controlled_buffer_4_out, controlled_buffer_5_out, controlled_buffer_6_out, controlled_buffer_7_out,
       controlled_buffer_8_out, controlled_buffer_9_out, controlled_buffer_10_out;

  and _0 (_0_out, ~x[0], ~x[1], ~x[2], ~x[3]);  // AND_Gate
  and _1 (_1_out, x[0], ~x[1], ~x[2], ~x[3]);  // AND_Gate
  and _2 (_2_out, ~x[0], x[1], ~x[2], ~x[3]);  // AND_Gate
  and _3 (_3_out, x[0], x[1], ~x[2], ~x[3]);  // AND_Gate
  and _4 (_4_out, ~x[0], ~x[1], x[2], ~x[3]);  // AND_Gate
  and _5 (_5_out, x[0], ~x[1], x[2], ~x[3]);  // AND_Gate
  and _6 (_6_out, ~x[0], x[1], x[2], ~x[3]);  // AND_Gate
  and _7 (_7_out, x[0], x[1], x[2], ~x[3]);  // AND_Gate
  and _8 (_8_out, ~x[0], ~x[1], ~x[2], x[3]);  // AND_Gate
  and _9 (_9_out, x[0], ~x[1], ~x[2], x[3]);  // AND_Gate
  assign controlled_buffer_1_out = _0_out ? 8'h7e : 8'bz;  // Controlled_Buffer controlled_buffer_1
  assign controlled_buffer_2_out = _1_out ? 8'h12 : 8'bz;  // Controlled_Buffer controlled_buffer_2
  assign controlled_buffer_3_out = _2_out ? 8'hbc : 8'bz;  // Controlled_Buffer controlled_buffer_3
  assign controlled_buffer_4_out = _3_out ? 8'hb6 : 8'bz;  // Controlled_Buffer controlled_buffer_4
  assign controlled_buffer_5_out = _4_out ? 8'hd2 : 8'bz;  // Controlled_Buffer controlled_buffer_5
  assign controlled_buffer_6_out = _5_out ? 8'he6 : 8'bz;  // Controlled_Buffer controlled_buffer_6
  assign controlled_buffer_7_out = _6_out ? 8'hee : 8'bz;  // Controlled_Buffer controlled_buffer_7
  assign controlled_buffer_8_out = _7_out ? 8'h32 : 8'bz;  // Controlled_Buffer controlled_buffer_8
  assign controlled_buffer_9_out = _8_out ? 8'hfe : 8'bz;  // Controlled_Buffer controlled_buffer_9
  assign controlled_buffer_10_out = _9_out ? 8'hf6 : 8'bz;  // Controlled_Buffer controlled_buffer_10
  Multiplexer #(.select(4), .width(8)) multiplexer_1 (
    .in0(controlled_buffer_1_out), .in1(controlled_buffer_2_out), .in2(controlled_buffer_3_out),
    .in3(controlled_buffer_4_out), .in4(controlled_buffer_5_out), .in5(controlled_buffer_6_out),
    .in6(controlled_buffer_7_out), .in7(controlled_buffer_8_out), .in8(controlled_buffer_9_out),
    .in9(controlled_buffer_10_out), .out(y), .sel(x), .en(1'b1));  // open: in10, in11, in12, in13, in14, in15
endmodule

module DAY (
  input  [2:0] x,
  output [15:0] y
);

  wire and_1_out, and_2_out, and_3_out, and_4_out, and_5_out, and_6_out, and_7_out;
  wire [15:0] controlled_buffer_1_out, controlled_buffer_2_out, controlled_buffer_3_out,
       controlled_buffer_4_out, controlled_buffer_5_out, controlled_buffer_6_out, controlled_buffer_7_out;

  and and_1 (and_1_out, ~x[0], ~x[1], ~x[2]);  // AND_Gate
  and and_2 (and_2_out, x[0], ~x[1], ~x[2]);  // AND_Gate
  and and_3 (and_3_out, ~x[0], x[1], ~x[2]);  // AND_Gate
  and and_4 (and_4_out, x[0], x[1], ~x[2]);  // AND_Gate
  and and_5 (and_5_out, ~x[0], ~x[1], x[2]);  // AND_Gate
  and and_6 (and_6_out, x[0], ~x[1], x[2]);  // AND_Gate
  and and_7 (and_7_out, ~x[0], x[1], x[2]);  // AND_Gate
  assign controlled_buffer_1_out = and_1_out ? 16'h7ada : 16'bz;  // Controlled_Buffer controlled_buffer_1
  assign controlled_buffer_2_out = and_2_out ? 16'hfecc : 16'bz;  // Controlled_Buffer controlled_buffer_2
  assign controlled_buffer_3_out = and_3_out ? 16'h6cf8 : 16'bz;  // Controlled_Buffer controlled_buffer_3
  assign controlled_buffer_4_out = and_4_out ? 16'hd2cc : 16'bz;  // Controlled_Buffer controlled_buffer_4
  assign controlled_buffer_5_out = and_5_out ? 16'h7acc : 16'bz;  // Controlled_Buffer controlled_buffer_5
  assign controlled_buffer_6_out = and_6_out ? 16'h6cee : 16'bz;  // Controlled_Buffer controlled_buffer_6
  assign controlled_buffer_7_out = and_7_out ? 16'hfe6c : 16'bz;  // Controlled_Buffer controlled_buffer_7
  Multiplexer #(.select(3), .width(16)) multiplexer_1 (
    .in0(controlled_buffer_1_out), .in1(controlled_buffer_2_out), .in2(controlled_buffer_3_out),
    .in3(controlled_buffer_4_out), .in4(controlled_buffer_5_out), .in5(controlled_buffer_6_out),
    .in6(controlled_buffer_7_out), .out(y), .sel(x), .en(1'b1));  // open: in7
endmodule

module tmp (
);

  wire A, B, counter_2_q, counter_3_q, \останов_часов ;
  wire [7:0] bit_extender_1_out, \откл_индикатора ;
  wire [15:0] bit_extender_2_out, \откл_индикатора_16бит ;

  Counter #(.width(1), .max('h1)) counter_1 (
    .D(1'b0), .count(B), .Q(\останов_часов ), .clk(B));  // open: load, carry, clr
  Counter #(.width(1), .max('h1)) counter_2 (.D(1'b0), .count(A), .Q(counter_2_q), .clk(A));  // open: load, carry, clr
  Counter #(.width(1), .max('h1)) counter_3 (.D(1'b0), .count(A), .Q(counter_3_q), .clk(A));  // open: load, carry, clr
  assign bit_extender_1_out = {{7{counter_2_q}}, counter_2_q};  // Bit_Extender bit_extender_1
  assign bit_extender_2_out = {{15{counter_3_q}}, counter_3_q};  // Bit_Extender bit_extender_2
  assign \откл_индикатора  = {8{1'b1}} ^ bit_extender_1_out;  // XOR_Gate xor_1, 8 bits wide
  assign \откл_индикатора_16бит  = {16{1'b1}} ^ bit_extender_2_out;  // XOR_Gate xor_2, 16 bits wide
endmodule

module am_and_pm (
  input  x,
  output [15:0] y
);

  wire not_1_out;
  wire [15:0] controlled_buffer_1_out, controlled_buffer_2_out;

  not not_1 (not_1_out, x);
  assign controlled_buffer_1_out = not_1_out ? 16'hf9db : 16'bz;  // Controlled_Buffer controlled_buffer_1
  assign controlled_buffer_2_out = x ? 16'hfbdb : 16'bz;  // Controlled_Buffer controlled_buffer_2
  Multiplexer #(.width(16)) multiplexer_1 (
    .in0(controlled_buffer_1_out), .in1(controlled_buffer_2_out), .out(y), .sel(x), .en(1'b1));
endmodule
